# Fritzing sketch Zombie Detector (saved by Fritzing 0.9.3b)
breadboards: 1

parts:
  Part1 = Arduino Uno (Rev3)
  hc-sr1 = hc-sr04
  J1 = Piezo Speaker
  LED2 = LED - 5mm [color="Red (633nm)" package="5 mm [THT]"]
  R1 = Resistor [tolerance=±5% resistance=330 package=THT]

nets:
  N1: Part1.D8, hc-sr1.Trig
  N2: Part1.D9_PWM, J1.pin2
  GND: Part1.GND, hc-sr1.GND, J1.pin1, LED2.cathode
  N3: Part1.D6_PWM, R1.Pin_1
  N4: Part1.D7, hc-sr1.Echo
  5V: Part1.5V, hc-sr1.VCC
  N5: LED2.anode, R1.Pin_0
